# Fritzing sketch tvb (saved by Fritzing 0.9.1b)
circuit board: 8.46667cm x 5.64444cm

parts:
  LED1 = LED - 5mm [color="Infrared (940nm)" package="5 mm [THT]"]
  Q1 = NPN-Transistor [package="TO92 [THT]"]
  Parte1 = Arduino Nano (Rev3.0)
  R1 = Resistor [tolerance=±5% resistance=220 package=THT]
  VCC1 = Battery block 9V

nets:
  N1: LED1.cathode, Q1.C
  N2: LED1.anode, Parte1.3V3
  N3: Q1.E, Parte1.GND, VCC1.-
  N4: Q1.B, R1.Pin_0
  N5: Parte1.D3, R1.Pin_1
  N6: Parte1.VIN, VCC1.+
